# Fritzing sketch pIoT (saved by Fritzing 0.8.7b)
breadboards: 2

parts:
  U2 = 2.4GHz Low Power Transceiver [package=qfn20]
  VCC1 = Battery  # not connected
  Part1 = FTDI Basic Programmer
  U3 = atmega328 [package=dip]
  R1 = Resistor [tolerance=±5% resistance=10k package=THT]
  C3 = Electrolytic Capacitor [capacitance=10µF package="200 mil [THT, electrolytic]"]
  C4 = Ceramic Capacitor [capacitance=22pF package="0603 [SMD, multilayer]"]

nets (from the breadboard view):
  N1: U2.VSS, Part1.CTS, C3.-
  N2: U2.CE, U3.D9_(PWM)
  N3: U2.CSN, U3.D10_(PWM)
  N4: U2.SCK, U3.D13
  N5: U2.MOSI, U3.D11_(PWM)
  N6: U2.MISO, U3.D12
  N7: U2.IRQ, U3.D2
  N8: U2.VDD, Part1.POWER, R1.Pin_0, C3.+
  N9: Part1.DTR, C4.0
  N10: Part1.RXI, U3.D1_(TX)
  N11: Part1.TXO, U3.D0_(RX)
  N12: U3.RESET, R1.Pin_1, C4.1
